# Fritzing sketch annoying.js (saved by Fritzing 0.9.3b)
breadboards: 1

parts:
  Part1 = Arduino Uno (Rev3)
  LED1 = LED - 5mm [color="Red (633nm)" package="5 mm [THT]"]
  J1 = Piezo Speaker
  LED2 = LED - 5mm [color="Green (555nm)" package="5 mm [THT]"]
  LED3 = smd LED [color="Blue (430nm)" package="0603 [SMD]"]
  LED4 = LED - 5mm [color="White (8000K)" package="5 mm [THT]"]
  LED5 = LED - 5mm [color="Yellow (585nm)" package="5 mm [THT]"]

nets:
  N1: Part1.D8, LED2.anode
  N2: Part1.D9_PWM, LED2.cathode
  N3: Part1.D10_PWM/SS, LED1.anode
  N4: Part1.D11_PWM/MOSI, LED1.cathode
  N5: Part1.D13/SCK, J1.pin2
  N6: Part1.D2, LED5.anode
  N7: Part1.D3_PWM, LED5.cathode
  N8: Part1.D4, LED4.anode
  N9: Part1.D5_PWM, LED4.cathode
  N10: Part1.D6_PWM, LED3.anode
  N11: Part1.D7, LED3.cathode
